# Fritzing sketch rc-car (saved by Fritzing 0.9.5d)

parts:
  BAT1 = 18650 battery holder [package=battery-18650-kit]
  BAT2 = 18650 battery holder [package=battery-18650-kit]
  M1 = RioRand LM2596
  U1 = ESP32S-HiLetgo [part_number=ESP32S-HiLetgo]
  M3 = DC Motor
  M2 = DC Motor
  M4 = DC Motor
  M5 = DC Motor
  Part1 = Motor Driver 1A Dual TB6612FNG

nets:
  N1: BAT1.+, BAT2.-
  N2: BAT1.-, M1.Pin_2, Part1.GND
  N3: BAT2.+, Part1.VM
  VIN: M1.Pin_3, U1.VIN, Part1.VCC
  N4: M1.Pin_4, U1.GND
  N5: U1.GPIO33, Part1.STBY
  N6: U1.GPIO25, Part1.PWMA
  N7: U1.GPIO26, Part1.AIN1
  N8: U1.GPIO27, Part1.AIN2
  N9: U1.GPIO14, Part1.PWMB
  N10: U1.GPIO16, Part1.BIN1
  N11: U1.GPIO17, Part1.BIN2
  N12: M3.pin_1, M4.pin_1, Part1.A01
  N13: M3.pin_2, M4.pin_2, Part1.A02
  N14: M2.pin_1, M5.pin_1, Part1.B01
  N15: M2.pin_2, M5.pin_2, Part1.B02

custom parts:
  18650 battery holder: 18650 Battery Holder identical to the dual battery version.
  ESP32S-HiLetgo: HiLetgo ESP-WROOM-32 ESP32 ESP-32S Development Board 2.4GHz Dual-Mode WiFi + Bluetooth Dual Cores Microcontroller The ESP32 integrated with Antenna switches, RF Balun, power amplifiers, low-noise amplifiers, filters, and management modules, and the entire solution occupies the least area of PCB. 2.4 GHz Wi-Fi plus Bluetooth dual-mode chip, with TSMC Ultra-low power consumption 40nm technology,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
